// Logisim project 16BitsAdder.circ as structural Verilog: 4 circuits, main circuit halfAdder
module halfAdder (
  input  A,
  input  B,
  output S,
  output CO
);

  xor xor_1 (S, A, B);
  and and_1 (CO, A, B);
endmodule

module fullAdder (
  input  CI,
  input  A,
  input  B,
  output S,
  output CO
);

  wire halfadder_1_co, halfadder_1_s, halfadder_2_co;

  halfAdder halfadder_1 (.A(A), .B(B), .S(halfadder_1_s), .CO(halfadder_1_co));
  halfAdder halfadder_2 (.A(CI), .B(halfadder_1_s), .S(S), .CO(halfadder_2_co));
  or or_1 (CO, halfadder_2_co, halfadder_1_co);
endmodule

module adderSubtractor8Bits (
  input  M,
  input  A0,
  input  B0,
  input  A1,
  input  B1,
  input  A2,
  input  B2,
  input  A3,
  input  B3,
  input  A4,
  input  B4,
  input  A5,
  input  B5,
  input  A6,
  input  B6,
  input  A7,
  input  B7,
  output S0,
  output S1,
  output S2,
  output S3,
  output S4,
  output S5,
  output S6,
  output S7,
  output C7
);

  wire fulladder_1_co, fulladder_2_co, fulladder_3_co, fulladder_4_co, fulladder_5_co, fulladder_6_co,
       fulladder_7_co, xor_1_out, xor_2_out, xor_3_out, xor_4_out, xor_5_out, xor_6_out, xor_7_out, xor_8_out;

  fullAdder fulladder_1 (.CI(M), .A(A0), .B(xor_1_out), .S(S0), .CO(fulladder_1_co));
  xor xor_1 (xor_1_out, B0, M);
  fullAdder fulladder_2 (.CI(fulladder_1_co), .A(A1), .B(xor_2_out), .S(S1), .CO(fulladder_2_co));
  xor xor_2 (xor_2_out, B1, M);
  fullAdder fulladder_3 (.CI(fulladder_2_co), .A(A2), .B(xor_3_out), .S(S2), .CO(fulladder_3_co));
  xor xor_3 (xor_3_out, B2, M);
  fullAdder fulladder_4 (.CI(fulladder_3_co), .A(A3), .B(xor_4_out), .S(S3), .CO(fulladder_4_co));
  xor xor_4 (xor_4_out, B3, M);
  fullAdder fulladder_5 (.CI(fulladder_4_co), .A(A4), .B(xor_5_out), .S(S4), .CO(fulladder_5_co));
  xor xor_5 (xor_5_out, B4, M);
  fullAdder fulladder_6 (.CI(fulladder_5_co), .A(A5), .B(xor_6_out), .S(S5), .CO(fulladder_6_co));
  xor xor_6 (xor_6_out, B5, M);
  fullAdder fulladder_7 (.CI(fulladder_6_co), .A(A6), .B(xor_7_out), .S(S6), .CO(fulladder_7_co));
  xor xor_7 (xor_7_out, B6, M);
  fullAdder fulladder_8 (.CI(fulladder_7_co), .A(A7), .B(xor_8_out), .S(S7), .CO(C7));
  xor xor_8 (xor_8_out, B7, M);
endmodule

module adderSubtractor16Bits (
  input  M0,
  input  in_2,
  input  in_3,
  input  in_4,
  input  in_5,
  input  in_6,
  input  in_7,
  input  in_8,
  input  in_9,
  input  in_10,
  input  in_11,
  input  in_12,
  input  in_13,
  input  in_14,
  input  in_15,
  input  in_16,
  input  in_17,
  input  in_18,
  input  in_19,
  input  in_20,
  input  in_21,
  input  in_22,
  input  in_23,
  input  in_24,
  input  in_25,
  input  in_26,
  input  in_27,
  input  in_28,
  input  in_29,
  input  in_30,
  input  in_31,
  input  in_32,
  input  in_33,
  output out_34,
  output out_35,
  output out_36,
  output out_37,
  output out_38,
  output out_39,
  output out_40,
  output out_41,
  output out_42,
  output out_43,
  output out_44,
  output out_45,
  output out_46,
  output out_47,
  output out_48,
  output out_49
);

  wire addersubtractor8bits_1_c7;

  adderSubtractor8Bits addersubtractor8bits_1 (
    .M(M0), .A0(in_2), .B0(in_3), .A1(in_4), .B1(in_5), .A2(in_6), .B2(in_7), .A3(in_8), .B3(in_9),
    .A4(in_10), .B4(in_11), .A5(in_12), .B5(in_13), .A6(in_14), .B6(in_15), .A7(in_16), .B7(in_17),
    .S0(out_34), .S1(out_35), .S2(out_36), .S3(out_37), .S4(out_38), .S5(out_39), .S6(out_40), .S7(out_41),
    .C7(addersubtractor8bits_1_c7));
  adderSubtractor8Bits addersubtractor8bits_2 (
    .M(addersubtractor8bits_1_c7), .A0(in_18), .B0(in_19), .A1(in_20), .B1(in_21), .A2(in_22), .B2(in_23),
    .A3(in_24), .B3(in_25), .A4(in_26), .B4(in_27), .A5(in_28), .B5(in_29), .A6(in_30), .B6(in_31),
    .A7(in_32), .B7(in_33), .S0(out_42), .S1(out_43), .S2(out_44), .S3(out_45), .S4(out_46), .S5(out_47),
    .S6(out_48), .S7(out_49));  // open: C7
endmodule
